// Logisim project lab5.circ as structural Verilog: 2 circuits, main circuit D триггер
module \D_триггер  (
  input  D,
  input  C,
  output Q0,
  output Q1
);

  wire nand_1_out, nand_2_out;

  nand nand_1 (nand_1_out, D, C);
  nand nand_2 (nand_2_out, nand_1_out, C);
  nand nand_3 (Q0, nand_1_out, Q1);
  nand nand_4 (Q1, Q0, nand_2_out);

  // Notes on the sheet:
  //   Схема D триггера, реализованная на ТТЛ элементах
endmodule

module \T_триггер  (
  input  C,
  input  T,
  output Q0,
  output Q1
);

  wire nand_1_out, nand_2_out;

  nand nand_1 (nand_1_out, C, T);
  nand nand_2 (nand_2_out, nand_1_out, T);
  nand nand_3 (Q0, nand_1_out, Q1);
  nand nand_4 (Q1, Q0, nand_2_out);

  // Notes on the sheet:
  //   Схема T триггера
endmodule
