// Logisim project lab6.circ as structural Verilog: 6 circuits, main circuit Схема сравнения
module \Схема_сравнения  (
  input  X1,
  input  X2,
  output Y
);

  wire HE_2_out, HE_out, \И_2_out , \И_out ;

  not HE (HE_out, X1);
  not HE_2 (HE_2_out, X2);
  and \u_И  (\И_out , HE_out, X2);
  and \u_И_2  (\И_2_out , X1, HE_2_out);
  or \u_ИЛИ  (Y, \И_out , \И_2_out );

  // Notes on the sheet:
  //   Схема сравнения
endmodule

module \Полусумматор  (
  input  X1,
  input  X2,
  output \Старший_разряд___перенос ,
  output \Младший_разряд 
);

  and \u_И  (\Старший_разряд___перенос , X1, X2);
  \Схема_сравнения  \u_Схема_сравнения  (.X1(X1), .X2(X2), .Y(\Младший_разряд ));

  // Notes on the sheet:
  //   Полусумматор
endmodule

// SM
module \Полный_сумматор  (
  input  X1,
  input  X2,
  input  Pi,
  output P,
  output S
);

  wire \Полусумматор_2_старший_разряд___перенос , \Полусумматор_младший_разряд ,
       \Полусумматор_старший_разряд___перенос ;

  \Полусумматор  \u_Полусумматор  (
    .X1(X1), .X2(X2), .\Старший_разряд___перенос (\Полусумматор_старший_разряд___перенос ),
    .\Младший_разряд (\Полусумматор_младший_разряд ));
  \Полусумматор  \u_Полусумматор_2  (
    .X1(\Полусумматор_младший_разряд ), .X2(Pi),
    .\Старший_разряд___перенос (\Полусумматор_2_старший_разряд___перенос ), .\Младший_разряд (S));
  or \u_Или  (P, \Полусумматор_старший_разряд___перенос , \Полусумматор_2_старший_разряд___перенос );

  // Notes on the sheet:
  //   Полный сумматор
  //   Перенос
  //   Младший разряд суммы
endmodule

module \_4_сумматора  (
  input  X4,
  input  Y4,
  input  X3,
  input  Y3,
  input  X2,
  input  Y2,
  input  X1,
  input  Y1,
  input  P0,
  output S5,
  output S4,
  output S3,
  output S2,
  output S1
);

  wire P1_p, P2_p, P3_p;

  \Полный_сумматор  P1 (.X1(X1), .X2(Y1), .Pi(P0), .P(P1_p), .S(S1));
  \Полный_сумматор  P2 (.X1(X2), .X2(Y2), .Pi(P1_p), .P(P2_p), .S(S2));
  \Полный_сумматор  P4 (.X1(X4), .X2(Y4), .Pi(P3_p), .P(S5), .S(S4));
  \Полный_сумматор  P3 (.X1(X3), .X2(Y3), .Pi(P2_p), .P(P3_p), .S(S3));

  // Notes on the sheet:
  //   4 сумматора
endmodule

module \Полусумматор__из_теоретического_раздела  (
  input  A,
  input  B,
  output S,
  output P
);

  wire not_1_out, \ИЛИ_out ;

  or \u_ИЛИ  (\ИЛИ_out , A, B);
  and \u_И  (P, A, B);
  not not_1 (not_1_out, P);
  and \u_И_2  (S, \ИЛИ_out , not_1_out);

  // Notes on the sheet:
  //   Полусумматор (из теоретического раздела)
endmodule

module \Сумматор__из_теоретического_раздела  (
  input  A,
  input  B,
  input  P_0,
  output P,
  output S
);

  wire not_1_out, \И_2_out , \И_3_out , \И_4_out , \И_5_out , \И_out , \ИЛИ_out ;

  and \u_И  (\И_out , A, B);
  and \u_И_2  (\И_2_out , A, P_0);
  and \u_И_3  (\И_3_out , B, P_0);
  or \u_ИЛИ  (\ИЛИ_out , A, B, P_0);
  and \u_И_4  (\И_4_out , A, B, P_0);
  or \u_ИЛИ_2  (P, \И_out , \И_2_out , \И_3_out );
  not not_1 (not_1_out, P);
  and \u_И_5  (\И_5_out , not_1_out, \ИЛИ_out );
  or \u_ИЛИ_3  (S, \И_5_out , \И_4_out );

  // Notes on the sheet:
  //   Cумматор (из теоретического раздела)
endmodule
